// Logisim project bfpa.circ as structural Verilog: 3 circuits, main circuit main
module main (
);

  wire and_1_out, and_2_out, and_3_out, and_4_out, and_5_out, and_6_out, and_7_out, and_8_out, and_9_out,
       clock_1_out, comparator_1_eq, comparator_2_eq, decoder_1_out2, not_1_out, or_1_out, or_2_out,
       s_r_ff_1_q, s_r_ff_2_qn;
  wire [2:0] controlled_buffer_1_out, decoder_1_out0, rom_1_data;
  wire [7:0] adder_1_out, counter_1_q, counter_2_q, counter_3_q, cstack_1_out, multiplexer_1_out,
       pull_resistor_1_node, subtractor_1_out;

  Pull_Resistor pull_resistor_1 (.node(pull_resistor_1_node));
  Counter counter_1 (.load(s_r_ff_1_q), .count(1'b1), .Q(counter_1_q), .clk(and_1_out));  // open: D, carry, clr
  and and_1 (and_1_out, or_1_out, and_3_out);
  or or_1 (or_1_out, and_2_out, and_5_out);
  Comparator comparator_1 (.a(pull_resistor_1_node), .b({8{1'b0}}), .eq(comparator_1_eq));  // open: gt, lt
  and and_2 (and_2_out, decoder_1_out2, rom_1_data[0], comparator_1_eq);
  and and_3 (and_3_out, ~decoder_1_out0[2], clock_1_out);  // AND_Gate
  Clock clock_1 (.out(clock_1_out));
  Comparator comparator_2 (.a(counter_1_q), .b({8{1'b0}}), .eq(comparator_2_eq));  // open: gt, lt
  and and_4 (and_4_out, comparator_2_eq, ~and_5_out);  // AND_Gate
  S_R_Flip_Flop #(.trigger("high")) s_r_ff_1 (
    .S(and_2_out), .clk(1'b1), .R(and_5_out), .Q(s_r_ff_1_q));  // open: Qn, preset, reset, en
  Counter #(.trigger("falling")) counter_2 (
    .load(rom_1_data[0]), .count(1'b1), .Q(counter_2_q), .clk(controlled_buffer_1_out[1]));  // open: D, carry, clr
  or or_2 (or_2_out, and_8_out, and_6_out);
  and and_5 (and_5_out, decoder_1_out2, ~rom_1_data[0], comparator_1_eq);  // AND_Gate
  cstack cstack_1 (.push(and_7_out), .d(counter_3_q), .pop(or_2_out), .out(cstack_1_out));
  not not_1 (not_1_out, and_6_out);
  and and_6 (and_6_out, ~comparator_1_eq, decoder_1_out2, and_3_out, rom_1_data[0], s_r_ff_2_qn);  // AND_Gate
  and and_7 (and_7_out, ~comparator_1_eq, decoder_1_out2, and_3_out, ~rom_1_data[0], s_r_ff_2_qn);  // AND_Gate
  and and_8 (and_8_out, comparator_1_eq, decoder_1_out2, and_3_out, rom_1_data[0], s_r_ff_2_qn);
  S_R_Flip_Flop #(.trigger("falling")) s_r_ff_2 (
    .S(and_5_out), .clk(and_3_out), .R(and_4_out), .Qn(s_r_ff_2_qn));  // open: Q, preset, reset, en
  RAM #(.bus("separate")) ram_1 (
    .addr(counter_2_q), .din(multiplexer_1_out), .data(pull_resistor_1_node), .clk(controlled_buffer_1_out[0]));  // open: str, sel, ld, clr
  // Probe on cstack_1_out
  Counter #(.trigger("falling")) counter_3 (
    .load(and_6_out), .D(cstack_1_out), .count(not_1_out), .Q(counter_3_q), .clk(and_3_out));  // open: carry, clr
  Adder adder_1 (.a(8'h1), .b(pull_resistor_1_node), .out(adder_1_out));  // open: cin, cout
  Multiplexer #(.width(8), .enable("false")) multiplexer_1 (
    .in0(adder_1_out), .in1(subtractor_1_out), .out(multiplexer_1_out), .sel(rom_1_data[0]));
  Subtractor subtractor_1 (.a(pull_resistor_1_node), .b(8'h1), .out(subtractor_1_out));  // open: bin, bout
  ROM #(.dataWidth(3)) rom_1 (.addr(counter_3_q), .data(rom_1_data));  // open: sel
  Decoder #(.select(2), .enable("false")) decoder_1 (
    .out0(decoder_1_out0[0]), .out1(decoder_1_out0[1]), .out2(decoder_1_out2), .out3(decoder_1_out0[2]),
    .sel(rom_1_data[2:1]));
  assign controlled_buffer_1_out = and_9_out ? decoder_1_out0 : 3'bz;  // Controlled_Buffer controlled_buffer_1
  Pull_Resistor pull_resistor_2 (.node(controlled_buffer_1_out));
  and and_9 (and_9_out, and_3_out, s_r_ff_2_qn);

  // Notes on the sheet:
  //   0b00x pointer value
  //   0b01x move pointer
  //   0b10x loop
  //   0b11x IO||halt
  //   contents of rom_1 (hex, n*v repeats v):
  //   0 0 2 0 0 0 3 4 1 2 4 2 0 2 0 3 3 1 5 2 4 1 3 0 2 5 3 3 5 7
endmodule

module bstack (
  input  push,
  input  [7:0] d,
  input  pop,
  output [7:0] out,
  output [7:0] delayed,
  output [7:0] optimal
);

  wire comparator_1_eq, comparator_1_gt, or_1_out, or_2_out, s_r_ff_1_q;
  wire [7:0] counter_1_q;

  Counter #(.trigger("falling")) counter_1 (
    .load(s_r_ff_1_q), .count(1'b1), .Q(counter_1_q), .clk(or_1_out));  // open: D, carry, clr
  or or_1 (or_1_out, push, pop);
  S_R_Flip_Flop #(.trigger("low")) s_r_ff_1 (
    .S(pop), .clk(1'b0), .R(push), .Q(s_r_ff_1_q));  // open: Qn, preset, reset, en
  RAM #(.bus("separate")) ram_1 (
    .addr(counter_1_q), .din(d), .data(out), .str(push), .clk(or_1_out));  // open: sel, ld, clr
  Register #(.trigger("falling")) register_1 (.D(out), .Q(delayed), .clk(or_1_out));  // open: en, clr
  or or_2 (or_2_out, comparator_1_gt, comparator_1_eq);
  Comparator comparator_1 (.a(out), .b(delayed), .gt(comparator_1_gt), .eq(comparator_1_eq));  // open: lt
  Multiplexer #(.width(8), .enable("false")) multiplexer_1 (.in0(delayed), .in1(out), .out(optimal), .sel(or_2_out));
endmodule

module cstack (
  input  push,
  input  [7:0] d,
  input  pop,
  output [7:0] out
);

  wire not_1_out, or_1_out;
  wire [7:0] counter_1_q, ram_1_data, register_1_q;

  or or_1 (or_1_out, pop, push);
  Counter counter_1 (.load(pop), .count(1'b1), .Q(counter_1_q), .clk(or_1_out));  // open: D, carry, clr
  Register #(.trigger("low")) register_1 (.D(d), .Q(register_1_q), .clk(push));  // open: en, clr
  not not_1 (not_1_out, push);
  RAM #(.bus("separate")) ram_1 (
    .addr(counter_1_q), .din(register_1_q), .data(ram_1_data), .clk(not_1_out));  // open: str, sel, ld, clr
  Register #(.trigger("low")) register_2 (.D(ram_1_data), .Q(out), .clk(or_1_out));  // open: en, clr
endmodule
