// Logisim project pong.circ as structural Verilog: 4 circuits, main circuit main
module main (
);

  wire and_2_out, button_1_out, button_2_out, clock_1_out, collider_1_bouncex, collider_1_bouncey,
       collider_1_hit_c, collider_1_hit_p, demultiplexer_1_out0, demultiplexer_1_out1, gpu_1_new_frame,
       j_k_ff_1_q, j_k_ff_2_q, j_k_ff_3_q, j_k_ff_4_q, j_k_ff_5_qn, or_1_out, or_2_out, or_3_out, or_4_out,
       or_5_out, pull_resistor_1_node, random_1_out, xor_1_out;
  wire [1:0] joystick_1_y;
  wire [3:0] counter_3_q, counter_4_q;
  wire [4:0] controller_1_out_4, counter_1_q, counter_2_q, gpu_1_rowraw;
  wire [31:0] dotmatrix_1_p4, gpu_1_data, gpu_1_row;

  or or_1 (or_1_out, and_2_out, or_2_out);
  Pull_Resistor pull_resistor_1 (.node(pull_resistor_1_node));
  or or_2 (or_2_out, button_2_out, pull_resistor_1_node);
  controller controller_1 (
    .reset(or_2_out), .joystik_y(joystick_1_y), .tick(gpu_1_new_frame), .out_4(controller_1_out_4));
  or or_3 (or_3_out, or_2_out, j_k_ff_3_q);
  xor xor_1 (xor_1_out, 1'b1, or_2_out);
  or or_4 (or_4_out, or_2_out, j_k_ff_4_q);
  J_K_Flip_Flop j_k_ff_1 (.J(1'b1), .clk(or_1_out), .K(1'b1), .Q(j_k_ff_1_q));  // open: Qn, preset, en, reset
  and and_1 (pull_resistor_1_node, or_5_out, clock_1_out);
  or or_5 (or_5_out, collider_1_hit_p, collider_1_hit_c);
  Counter #(.width(5), .max('h1f)) counter_1 (
    .load(or_3_out), .D(5'b10000), .count(xor_1_out), .Q(counter_1_q), .clk(or_1_out));  // open: carry, clr
  Counter #(.width(5), .max('h1f)) counter_2 (
    .load(or_4_out), .D(5'b10000), .count(xor_1_out), .Q(counter_2_q), .clk(j_k_ff_1_q));  // open: carry, clr
  J_K_Flip_Flop j_k_ff_2 (.J(1'b1), .clk(button_1_out), .K(1'b1), .Q(j_k_ff_2_q));  // open: Qn, preset, en, reset
  // Probe on controller_1_out_4
  Clock clock_1 (.out(clock_1_out));
  collider collider_1 (
    .bx(counter_1_q), .by(counter_2_q), .py(controller_1_out_4), .cy(counter_2_q),
    .bouncey(collider_1_bouncey), .hit_p(collider_1_hit_p), .bouncex(collider_1_bouncex),
    .hit_c(collider_1_hit_c));
  J_K_Flip_Flop j_k_ff_3 (.J(1'b1), .clk(collider_1_bouncex), .K(1'b1), .Q(j_k_ff_3_q));  // open: Qn, preset, en, reset
  J_K_Flip_Flop j_k_ff_4 (
    .J(1'b1), .clk(collider_1_bouncey), .K(1'b1), .Q(j_k_ff_4_q), .preset(demultiplexer_1_out0),
    .reset(demultiplexer_1_out1));  // open: Qn, en
  Random #(.width(1)) random_1 (.clk(button_2_out), .out(random_1_out));  // open: next, clr
  Demultiplexer #(.enable("false")) demultiplexer_1 (
    .out0(demultiplexer_1_out0), .out1(demultiplexer_1_out1), .in(button_2_out), .sel(random_1_out));
  and and_2 (and_2_out, gpu_1_new_frame, j_k_ff_2_q);
  Pull_Resistor pull_resistor_2 (.node(counter_2_q));
  // Probe on counter_2_q
  Counter #(.width(4), .max('hf)) counter_3 (
    .Q(counter_3_q), .clk(collider_1_hit_c), .clr(button_2_out));  // open: load, D, count, carry
  Counter #(.width(4), .max('hf)) counter_4 (
    .Q(counter_4_q), .clk(collider_1_hit_p), .clr(button_2_out));  // open: load, D, count, carry
  J_K_Flip_Flop j_k_ff_5 (.J(1'b1), .clk(clock_1_out), .K(1'b1), .Qn(j_k_ff_5_qn));  // open: Q, preset, en, reset
  GPU gpu_1 (
    .clear(or_2_out), .clock(clock_1_out), .p_y(controller_1_out_4), .c_y(counter_2_q), .by(counter_2_q),
    .bx(counter_1_q), .row(gpu_1_row), .data(gpu_1_data), .rowraw(gpu_1_rowraw), .new_frame(gpu_1_new_frame));  // open: syncer
  // Probe on gpu_1_rowraw
  Hex_Digit_Display hex_digit_display_1 (.value(counter_4_q));  // open: dp
  Hex_Digit_Display hex_digit_display_2 (.value(counter_3_q));  // open: dp
  // DotMatrix #(.inputtype("select"), .matrixcols(32), .matrixrows(32), .persist(256)) dotmatrix_1: pin names not known; wires that end beside it: j_k_ff_5_qn, gpu_1_data, gpu_1_row, dotmatrix_1_p4
  Button button_1 (.out(button_1_out));
  Joystick #(.bits(2)) joystick_1 (.y(joystick_1_y));  // open: x
  Button button_2 (.out(button_2_out));
endmodule

module GPU (
  input  clear,
  input  clock,
  input  [4:0] p_y,
  input  [4:0] c_y,
  input  [4:0] by,
  input  [4:0] bx,
  output [31:0] row,
  output [31:0] data,
  output syncer,
  output [4:0] rowraw,
  output new_frame
);

  wire comparator_1_lt, comparator_2_gt, comparator_3_lt, comparator_4_gt, comparator_5_lt, comparator_6_gt,
       j_k_ff_1_q, j_k_ff_1_qn, pull_resistor_1_node;
  wire [0:0] pull_resistor_3_node;
  wire [1:0] pull_resistor_2_node;
  wire [2:0] pull_resistor_4_node, pull_resistor_5_node, pull_resistor_7_node, pull_resistor_9_node;
  wire [2:2] nor_3_out;
  wire [7:0] adder_1_out, adder_2_out, adder_3_out, subtractor_1_out, subtractor_2_out, subtractor_3_out;
  wire [28:0] pull_resistor_10_node;
  wire [31:0] or_1_out, shifter_1_out;
  wire [31:1] nor_1_out;

  Pull_Resistor #(.pull(1)) pull_resistor_1 (.node(pull_resistor_1_node));
  J_K_Flip_Flop j_k_ff_1 (
    .J(pull_resistor_1_node), .clk(clock), .K(pull_resistor_1_node), .Q(j_k_ff_1_q), .Qn(j_k_ff_1_qn),
    .reset(clear));  // open: preset, en
  Pull_Resistor pull_resistor_2 (.node(pull_resistor_2_node));
  Pull_Resistor pull_resistor_3 (.node(pull_resistor_3_node[0]));
  Pull_Resistor pull_resistor_4 (.node(pull_resistor_4_node));
  Counter #(.width(5), .max('h1f)) counter_1 (
    .Q(rowraw), .carry(new_frame), .clk(j_k_ff_1_q), .clr(clear));  // open: load, D, count
  Pull_Resistor pull_resistor_5 (.node(pull_resistor_5_node));
  Subtractor subtractor_1 (
    .a({pull_resistor_2_node, p_y, pull_resistor_3_node[0]}), .b(8'h3), .out(subtractor_1_out));  // open: bin, bout
  Adder adder_1 (
    .a({pull_resistor_2_node, p_y, pull_resistor_3_node[0]}), .b(8'h4), .out(adder_1_out));  // open: cin, cout
  Subtractor subtractor_2 (.a({pull_resistor_4_node, c_y}), .b(8'h3), .out(subtractor_2_out));  // open: bin, bout
  Adder adder_2 (.a({pull_resistor_4_node, c_y}), .b(8'h4), .out(adder_2_out));  // open: cin, cout
  assign or_1_out = shifter_1_out | {{2{nor_1_out[31]}}, nor_1_out[29:1], nor_1_out[1]};  // OR_Gate or_1, 32 bits wide
  Comparator comparator_1 (
    .a({pull_resistor_5_node, rowraw}), .b(subtractor_1_out), .lt(comparator_1_lt));  // open: gt, eq
  nor nor_1 (nor_1_out[1], comparator_1_lt, comparator_2_gt);
  Comparator comparator_2 (.a({pull_resistor_5_node, rowraw}), .b(adder_1_out), .gt(comparator_2_gt));  // open: eq, lt
  Pull_Resistor pull_resistor_6 (.node(nor_1_out[29:2]));
  Comparator comparator_3 (
    .a({pull_resistor_5_node, rowraw}), .b(subtractor_2_out), .lt(comparator_3_lt));  // open: gt, eq
  nor nor_2 (nor_1_out[31], comparator_3_lt, comparator_4_gt);
  Comparator comparator_4 (.a({pull_resistor_5_node, rowraw}), .b(adder_2_out), .gt(comparator_4_gt));  // open: eq, lt
  Decoder #(.select(5), .disabled(0), .enable("false")) decoder_1 (
    .out0(row[31]), .out1(row[30]), .out2(row[29]), .out3(row[28]), .out4(row[27]), .out5(row[26]),
    .out6(row[25]), .out7(row[24]), .out8(row[23]), .out9(row[22]), .out10(row[21]), .out11(row[20]),
    .out12(row[19]), .out13(row[18]), .out14(row[17]), .out15(row[16]), .out16(row[15]), .out17(row[14]),
    .out18(row[13]), .out19(row[12]), .out20(row[11]), .out21(row[10]), .out22(row[9]), .out23(row[8]),
    .out24(row[7]), .out25(row[6]), .out26(row[5]), .out27(row[4]), .out28(row[3]), .out29(row[2]),
    .out30(row[1]), .out31(row[0]), .sel(rowraw));
  Pull_Resistor pull_resistor_7 (.node(pull_resistor_7_node));
  Pull_Resistor pull_resistor_8 (.node(j_k_ff_1_q));
  Pull_Resistor pull_resistor_9 (.node(pull_resistor_9_node));
  Subtractor subtractor_3 (.a({pull_resistor_7_node, by}), .b(8'h1), .out(subtractor_3_out));  // open: bin, bout
  Adder adder_3 (.a({pull_resistor_7_node, by}), .b(8'h1), .out(adder_3_out));  // open: cin, cout
  Comparator comparator_5 (
    .a({pull_resistor_9_node, rowraw}), .b(subtractor_3_out), .lt(comparator_5_lt));  // open: gt, eq
  Comparator comparator_6 (.a({pull_resistor_9_node, rowraw}), .b(adder_3_out), .gt(comparator_6_gt));  // open: eq, lt
  Pull_Resistor pull_resistor_10 (.node(pull_resistor_10_node));
  nor nor_3 (nor_3_out[2], comparator_5_lt, comparator_6_gt);
  Shifter #(.width(32)) shifter_1 (.in({pull_resistor_10_node, {3{nor_3_out[2]}}}), .\dist (bx), .out(shifter_1_out));
  Pull_Resistor pull_resistor_11 (.node(data));
  Transistor #(.\type ("n"), .gate("br"), .width(32)) transistor_1 (.in(or_1_out), .out(data), .gate(j_k_ff_1_qn));
  // DotMatrix #(.inputtype("select"), .matrixcols(32), .matrixrows(32), .persist(128), .dotshape("circle")) dotmatrix_1: pin names not known; wires that end beside it: data, row

  assign syncer = clear;

  // Notes on the sheet:
  //   offtick |--| line
  //   new frame
  //   data |--| write
endmodule

module collider (
  input  [4:0] bx,
  input  [4:0] by,
  input  [4:0] py,
  input  [4:0] cy,
  output bouncey,
  output hit_p,
  output bouncex,
  output hit_c
);

  wire and_2_out, and_4_out, comparator_1_lt, comparator_2_gt, comparator_3_lt, comparator_4_gt,
       comparator_5_eq, comparator_6_eq, comparator_7_eq, comparator_7_lt, comparator_8_eq, comparator_8_gt,
       nor_1_out, nor_2_out;
  wire [2:0] pull_resistor_1_node, pull_resistor_2_node, pull_resistor_3_node, pull_resistor_4_node;
  wire [7:0] adder_1_out, adder_2_out, shifter_1_out, subtractor_1_out, subtractor_2_out;

  Pull_Resistor pull_resistor_1 (.node(pull_resistor_1_node));
  Pull_Resistor pull_resistor_2 (.node(pull_resistor_2_node));
  Pull_Resistor pull_resistor_3 (.node(pull_resistor_3_node));
  Pull_Resistor pull_resistor_4 (.node(pull_resistor_4_node));
  // Probe on shifter_1_out
  Shifter shifter_1 (.in({pull_resistor_3_node, py}), .\dist (3'b001), .out(shifter_1_out));
  Subtractor subtractor_1 (.a(shifter_1_out), .b(8'h3), .out(subtractor_1_out));  // open: bin, bout
  Adder adder_1 (.a(shifter_1_out), .b(8'h4), .out(adder_1_out));  // open: cin, cout
  Subtractor subtractor_2 (.a({pull_resistor_4_node, cy}), .b(8'h3), .out(subtractor_2_out));  // open: bin, bout
  Adder adder_2 (.a({pull_resistor_4_node, cy}), .b(8'h4), .out(adder_2_out));  // open: cin, cout
  Comparator comparator_1 (.a({pull_resistor_2_node, by}), .b(subtractor_1_out), .lt(comparator_1_lt));  // open: gt, eq
  Comparator comparator_2 (.a({pull_resistor_2_node, by}), .b(adder_1_out), .gt(comparator_2_gt));  // open: eq, lt
  Comparator comparator_3 (.a({pull_resistor_2_node, by}), .b(subtractor_2_out), .lt(comparator_3_lt));  // open: gt, eq
  Comparator comparator_4 (.a({pull_resistor_2_node, by}), .b(adder_2_out), .gt(comparator_4_gt));  // open: eq, lt
  nor nor_1 (nor_1_out, comparator_1_lt, comparator_2_gt);
  nor nor_2 (nor_2_out, comparator_3_lt, comparator_4_gt);
  Comparator comparator_5 (.a({pull_resistor_2_node, by}), .b(8'h3), .eq(comparator_5_eq));  // open: gt, lt
  Comparator comparator_6 (.a({pull_resistor_2_node, by}), .b(8'h1e), .eq(comparator_6_eq));  // open: gt, lt
  Comparator comparator_7 (
    .a({pull_resistor_1_node, bx}), .b(8'h2), .eq(comparator_7_eq), .lt(comparator_7_lt));  // open: gt
  Comparator comparator_8 (
    .a({pull_resistor_1_node, bx}), .b(8'h1b), .gt(comparator_8_gt), .eq(comparator_8_eq));  // open: lt
  or or_1 (bouncey, comparator_5_eq, comparator_6_eq);
  and and_1 (hit_p, comparator_7_lt, nor_1_out);
  and and_2 (and_2_out, comparator_7_eq, nor_1_out);
  and and_3 (hit_c, comparator_8_gt, nor_2_out);
  and and_4 (and_4_out, comparator_8_eq, nor_2_out);
  or or_2 (bouncex, and_2_out, and_4_out);
endmodule

module controller (
  input  reset,
  input  [1:0] joystik_y,
  input  tick,
  output [4:0] out_4
);

  wire and_1_out, and_2_out, and_3_out, buffer_1_out, comparator_1_gt, comparator_2_lt, or_1_out, or_2_out,
       or_3_out, xor_1_out;

  // Probe on joystik_y
  and and_1 (and_1_out, joystik_y[0], comparator_1_gt, ~joystik_y[1]);  // AND_Gate
  and and_2 (and_2_out, joystik_y[1], comparator_2_lt, joystik_y[0]);
  buf buffer_1 (buffer_1_out, reset);
  or or_1 (or_1_out, reset, and_1_out);
  xor xor_1 (xor_1_out, reset, 1'b1);
  or or_2 (or_2_out, and_1_out, and_2_out);
  and and_3 (and_3_out, or_2_out, tick);
  or or_3 (or_3_out, and_3_out, buffer_1_out);
  Counter #(.width(5), .max('h1f)) counter_1 (
    .load(or_1_out), .D(5'b01000), .count(xor_1_out), .Q(out_4), .clk(or_3_out));  // open: carry, clr
  Comparator #(.width(5)) comparator_1 (.a(out_4), .b(5'b00010), .gt(comparator_1_gt));  // open: eq, lt
  Comparator #(.width(5)) comparator_2 (.a(out_4), .b(5'b01110), .lt(comparator_2_lt));  // open: gt, eq
endmodule
